// Logisim project RISC_V_32bit_ALU.circ as structural Verilog: 1 circuit, main circuit ALU
module ALU (
  input  [31:0] A,
  input  [31:0] B,
  input  [4:0] Amount_To_Shift,
  input  [11:0] twelve_bit_input,
  input  [19:0] Immediate,
  input  [31:0] PC,
  input  [31:0] Instruction,
  output [31:0] Result
);

  wire comparator_1_lt, comparator_2_lt, comparator_3_eq, comparator_4_eq, comparator_5_eq, comparator_6_eq,
       comparator_7_eq, comparator_8_eq, comparator_9_eq, comparator_10_eq, comparator_11_eq,
       comparator_12_eq, comparator_13_eq, comparator_14_eq;
  wire [3:0] priority_encoder_1_out;
  wire [31:0] adder_1_out, adder_2_out, and_1_out, bit_extender_1_out, bit_extender_2_out, or_1_out,
       shifter_1_out, shifter_2_out, shifter_3_out, subtractor_1_out, xor_1_out;

  Adder #(.width(32)) adder_1 (.a(A), .b(B), .out(adder_1_out));  // open: cin, cout
  Subtractor #(.width(32)) subtractor_1 (.a(A), .b(B), .out(subtractor_1_out));  // open: bin, bout
  Shifter #(.width(32)) shifter_1 (.in(A), .\dist (Amount_To_Shift), .out(shifter_1_out));
  assign bit_extender_1_out = {{31{comparator_1_lt}}, comparator_1_lt};  // Bit_Extender bit_extender_1
  Comparator #(.width(32)) comparator_1 (.a(A), .b(B), .lt(comparator_1_lt));  // open: gt, eq
  assign bit_extender_2_out = {{31{comparator_2_lt}}, comparator_2_lt};  // Bit_Extender bit_extender_2
  Comparator #(.mode("unsigned"), .width(32)) comparator_2 (.a(A), .b(B), .lt(comparator_2_lt));  // open: gt, eq
  assign xor_1_out = A ^ B;  // XOR_Gate xor_1, 32 bits wide
  Shifter #(.shift("lr"), .width(32)) shifter_2 (.in(A), .\dist (Amount_To_Shift), .out(shifter_2_out));
  Shifter #(.shift("ar"), .width(32)) shifter_3 (.in(A), .\dist (Amount_To_Shift), .out(shifter_3_out));
  assign or_1_out = A | B;  // OR_Gate or_1, 32 bits wide
  assign and_1_out = A & B;  // AND_Gate and_1, 32 bits wide
  Adder #(.width(32)) adder_2 (.a({Immediate, twelve_bit_input}), .b(PC), .out(adder_2_out));  // open: cin, cout
  Comparator #(.width(10)) comparator_3 (
    .a({Instruction[31:25], Instruction[14:12]}), .b({10{1'b0}}), .eq(comparator_3_eq));  // open: gt, lt
  Comparator #(.width(10)) comparator_4 (
    .a({Instruction[31:25], Instruction[14:12]}), .b(10'h100), .eq(comparator_4_eq));  // open: gt, lt
  Comparator #(.width(10)) comparator_5 (
    .a({Instruction[31:25], Instruction[14:12]}), .b(10'h1), .eq(comparator_5_eq));  // open: gt, lt
  Comparator #(.width(10)) comparator_6 (
    .a({Instruction[31:25], Instruction[14:12]}), .b(10'h2), .eq(comparator_6_eq));  // open: gt, lt
  Comparator #(.width(10)) comparator_7 (
    .a({Instruction[31:25], Instruction[14:12]}), .b(10'h3), .eq(comparator_7_eq));  // open: gt, lt
  Comparator #(.width(10)) comparator_8 (
    .a({Instruction[31:25], Instruction[14:12]}), .b(10'h4), .eq(comparator_8_eq));  // open: gt, lt
  Comparator #(.width(10)) comparator_9 (
    .a({Instruction[31:25], Instruction[14:12]}), .b(10'h5), .eq(comparator_9_eq));  // open: gt, lt
  Comparator #(.width(10)) comparator_10 (
    .a({Instruction[31:25], Instruction[14:12]}), .b(10'h105), .eq(comparator_10_eq));  // open: gt, lt
  Comparator #(.width(10)) comparator_11 (
    .a({Instruction[31:25], Instruction[14:12]}), .b(10'h6), .eq(comparator_11_eq));  // open: gt, lt
  Comparator #(.width(10)) comparator_12 (
    .a({Instruction[31:25], Instruction[14:12]}), .b(10'h7), .eq(comparator_12_eq));  // open: gt, lt
  Comparator #(.width(7)) comparator_13 (.a(Instruction[6:0]), .b(7'b0110111), .eq(comparator_13_eq));  // open: gt, lt
  Comparator #(.width(7)) comparator_14 (.a(Instruction[6:0]), .b(7'b0010111), .eq(comparator_14_eq));  // open: gt, lt
  Multiplexer #(.select(4), .width(32)) multiplexer_1 (
    .in0(adder_1_out), .in1(subtractor_1_out), .in2(shifter_1_out), .in3(bit_extender_1_out),
    .in4(bit_extender_2_out), .in5(xor_1_out), .in6(shifter_2_out), .in7(shifter_3_out), .in8(or_1_out),
    .in9(and_1_out), .in10({Immediate, twelve_bit_input}), .in11(adder_2_out), .out(Result),
    .sel(priority_encoder_1_out));  // open: in12, in13, in14, in15
  Priority_Encoder #(.select(4)) priority_encoder_1 (
    .in0(comparator_3_eq), .in1(comparator_4_eq), .in2(comparator_5_eq), .in3(comparator_6_eq),
    .in4(comparator_7_eq), .in5(comparator_8_eq), .in6(comparator_9_eq), .in7(comparator_10_eq),
    .in8(comparator_11_eq), .in9(comparator_12_eq), .in10(comparator_13_eq), .in11(comparator_14_eq),
    .out(priority_encoder_1_out));  // open: in12, in13, in14, in15, gs, en_out, en_in

  // Notes on the sheet:
  //   Opcode
  //   Function 3
  //   Function 7
  //   Adder
  //   Subtractor
  //   SLL
  //   SLT
  //   SLTU
  //   SRL
  //   SRA
  //   XOR
  //   OR
  //   AND
  //   LUI
  //   AUIPC
endmodule
